# Fritzing sketch Alreg (saved by Fritzing 0.7.1b)
breadboards: 1

parts:
  Arduino1 = Arduino
  IC1 = H-Bridge [package=THT]
  VCC1 = Battery block 9V
  R1 = Resistor [tolerance=±5% resistance=4.7k package=THT]
  Q2 = Temperature sensor [package="TO92 [THT]"]
  Parte1 = Barometric Pressure Sensor - BMP085 Breakout
  LED1 = LED - 5mm [color="Red (633nm)" package="5 mm [THT]"]
  R2 = Resistor [tolerance=±5% resistance=220 package=THT]
  R3 = Resistor [tolerance=±5% resistance=110 package=THT]
  R4 = Resistor [tolerance=±5% resistance=220 package=THT]
  C1 = Electrolytic Capacitor [capacitance=100µF voltage=25V package="100 mil [THT, electrolytic]"]

nets:
  N1: Arduino1.D12, R1.Pin_1, Q2.DQ
  N2: Arduino1.D9, R4.Pin_1
  N3: Arduino1.D8, R3.Pin_0
  N4: Arduino1.D6, R2.Pin_1
  N5: Arduino1.D4, IC1.2A
  N6: Arduino1.D3, IC1.1A
  N7: Arduino1.D2, IC1.1_2EN
  N8: Arduino1.RST, C1.-
  3V3: Arduino1.3V3, Parte1.VCC
  +5V: Arduino1.+5V, IC1.VCC1, R1.Pin_0, Q2.Vdd
  GND: Arduino1.GND, IC1.GND1, IC1.GND2, IC1.GND3, IC1.GND4, VCC1.-, Q2.GND, Parte1.GND, LED1.cathode, C1.+
  N9: Arduino1.VIN, IC1.VCC2, VCC1.+
  N10: Arduino1.A0, R4.Pin_0
  N11: Arduino1.A4, Parte1.SDA
  N12: Arduino1.A5, Parte1.SCL
  N13: LED1.anode, R2.Pin_0

notes:
  Salida Solenoide
  One Wire
  Humedad del suelo

custom parts:
  Temperature sensor: Dellas temperature sensor
